# Fritzing sketch ESP32ToProcessing (saved by Fritzing 0.9.4)
breadboards: 1

parts:
  Part1 = Adafruit HUZZAH32 ESP32 Feather [part_number="Adafruit #3405"]
  LED1 = LED - 5mm [color="Yellow (595nm)" package="5 mm [THT]"]
  R1_(LED) = Resistor [tolerance=±5% resistance=220 package=THT]
  R3_(LDR) = Resistor [tolerance=±5% resistance=220 package=THT]
  R2_(Switch) = Resistor [tolerance=±5% resistance=220 package=THT]
  Switch = Pushbutton [package=THT]
  LDR = Photocell (LDR) [package=THT]

nets:
  N1: Part1.A2_I34, R3_(LDR).Pin_1, LDR.pin_0
  N2: Part1.GND, LED1.anode, R3_(LDR).Pin_0, R2_(Switch).Pin_1, LDR.pin_1
  N3: Part1.3.3V, Switch.leg0
  N4: Part1.IO12_A11, R2_(Switch).Pin_0, Switch.leg1
  N5: Part1.IO33_A9, LED1.cathode, R1_(LED).Pin_0, R1_(LED).Pin_1
